# Fritzing sketch impreso_iot_GND (saved by Fritzing 0.9.3b)
circuit board: 8.42392cm x 9.77332cm
breadboards: 1

parts:
  Argon = Particle Argon
  J1 = female pin header, 1 pin [form="♀ (female)"]
  R1 = Resistor [tolerance=±5% resistance=12.2k package=THT]
  LED = female pin header, 6 pins [form="♀ (female)"]
  Panel = female pin header, 6 pins [form="♀ (female)"]
  R3 = Resistor [tolerance=±5% resistance=1k package=THT]
  J2 = female pin header, 1 pin [form="♀ (female)"]
  J3 = female pin header, 1 pin [form="♀ (female)"]
  J4 = female pin header, 1 pin [form="♀ (female)"]
  GNDs = Screw terminal - 2 pins [package=THT]
  R4 = Resistor [tolerance=±5% resistance=12.2k package=THT]
  Q1 = NPN-Transistor [package="TO92 [THT]"]
  R5 = Resistor [tolerance=±5% resistance=1k package=THT]
  IR_led = Screw terminal - 2 pins [package=THT]
  R6 = Resistor [tolerance=±5% resistance=100 package=THT]
  IC2 = IC, DIP package, 14 pins [chip_label=LM324]
  Bateria = female pin header, 6 pins [form="♀ (female)"]
  R2 = Resistor [tolerance=±5% resistance=1k package=THT]

nets:
  VCC: Argon.3.3V, LED.pin6, Panel.pin6, Bateria.pin6
  GND: Argon.GND, J1.pin1, LED.pin5, Panel.pin5, J3.pin1, GNDs.pin1, Q1.E, IC2.pin11, Bateria.pin5, R2.Pin_1
  ADC led: Argon.A0, R3.Pin_0, IC2.pin1
  IR pin: Argon.A5, R5.Pin_0
  SDA: Argon.SDA, LED.pin3, Panel.pin3, Bateria.pin3
  SCL: Argon.SCL, LED.pin4, Panel.pin4, Bateria.pin4
  v usb: Argon.VUSB, J4.pin1, IR_led.pin1, IC2.pin4
  v led +: R1.Pin_0, LED.pin1
  N1: R1.Pin_1, IC2.pin3, R2.Pin_0
  v led -: LED.pin2
  v pan +: Panel.pin1
  v pan -: Panel.pin2
  N2: R3.Pin_1, R4.Pin_0, IC2.pin2
  v bat +: J2.pin1, Bateria.pin1
  GND led: GNDs.pin2, R4.Pin_1
  N3: Q1.B, R5.Pin_1
  N4: Q1.C, R6.Pin_0
  N5: IR_led.pin2, R6.Pin_1
  v bat -: Bateria.pin2

custom parts:
  Particle Argon: The Argon is a powerful Wi-Fi enabled development board that can act as either a standalone Wi-Fi endpoint or Wi-Fi enabled gateway for Particle Mesh networks. It is based on the Nordic nRF52840 and has built-in battery charging circuitry so it’s easy to connect a Li-Po and deploy your local network in minutes. The Argon is great for connecting existing projects to the Particle Device Cloud or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
